# Fritzing sketch thermal gun (saved by Fritzing 0.9.4)
breadboards: 1

parts:
  Part1 = Arduino Nano (Rev3.0)
  J1 = Piezo Speaker
  R1 = Resistor [tolerance=±5% resistance=330 package="2512 [SMD]"]
  R2 = Resistor [tolerance=±5% resistance=10k package="2512 [SMD]"]
  R3 = Resistor [tolerance=±5% resistance=10k package="2512 [SMD]"]
  R4 = Resistor [tolerance=±5% resistance=10k package="2512 [SMD]"]
  R5 = Resistor [tolerance=±5% resistance=10k package="2512 [SMD]"]
  R6 = Resistor [tolerance=±5% resistance=10k package="2512 [SMD]"]
  S1 = Round Pushbutton
  R7 = Resistor [tolerance=±5% resistance=330 package="2512 [SMD]"]
  U1 = Battery Holders [package=lipo-1100mAh]
  TP1 = TP4056 [chip_label=TP4056 package="DIP (Dual Inline) [THT]"]
  U2 = MLX90614 [package=to-39]
  Nokia_5110_LCD_Module1 = Nokia 5110 LCD

nets:
  N1: Part1.D2, S1.leg0
  N2: Part1.D3, R2.Pin_0
  N3: Part1.D4, R3.Pin_0
  N4: Part1.D5, R4.Pin_0
  N5: Part1.D6, R5.Pin_0
  N6: Part1.D7, R6.Pin_0
  N7: Part1.D8, J1.pin2
  VDD: Part1.A5, Part1.A4, U2.VDD, U2.VSS
  N8: Part1.A2, U1.+
  N9: J1.pin1, S1.leg1, R7.Pin_0, U1.-, TP1.pin3, TP1.pin4, TP1.pin5, U2.SCL_VZ, U2.PWM_SDA, Nokia_5110_LCD_Module1.GND
  N10: R1.Pin_1, Nokia_5110_LCD_Module1.BL
  N11: R2.Pin_1, Nokia_5110_LCD_Module1.CLK
  N12: R3.Pin_1, Nokia_5110_LCD_Module1.Din
  N13: R4.Pin_1, Nokia_5110_LCD_Module1.D/C
  N14: R5.Pin_1, Nokia_5110_LCD_Module1.CE
  N15: R6.Pin_1, Nokia_5110_LCD_Module1.RST

notes:
  SDA TO A4
  SCL TO A5
  NOTE

custom parts:
  TP4056: A DIP stand-in part for whatever IC you want. With 6 pins on a 300mil dual inline package (DIP) footprint.
  Nokia 5110 LCD: Nokia 5110 Graphic 84*48 LCD module <Blue Version>
